# Fritzing sketch pi-sensor-board (saved by Fritzing 0.8.7b)
circuit board: 5.24543cm x 3.81907cm
breadboards: 1

parts:
  BMP1 = BMP085 Breakout
  Pi1 = Adafruit Pi Cobbler
  DHT1 = DHT22 Humidity and Temperature Sensor
  R1 = Resistor [tolerance=±5% resistance=4.7 package=THT]

nets:
  VIN: BMP1.VIN, Pi1.3V3, DHT1.VDD, R1.Pin_1
  N1: BMP1.SCL, Pi1.SCL0
  N2: BMP1.SDA, Pi1.SDA0
  GND: BMP1.GND, Pi1.GND, DHT1.GND
  N3: Pi1.#4, DHT1.DATA, R1.Pin_0

custom parts:
  BMP085 Breakout: A breakout for the BMP085 barometric pressure and temperature sensor
  Adafruit Pi Cobbler: Adafruit Pi Cobbler GPIO Breakout for Raspberry Pi
